# Fritzing sketch Projet (saved by Fritzing 0.9.9b)
breadboards: 1

parts:
  U1 = OP27 - Low Noise, Precision Op Amp [part_number=OP27]
  U2 = OP27 - Low Noise, Precision Op Amp [part_number=OP27]
  P1 = S1133 Si Photodiode [package="8mm Ceramic [THT]"]
  Composant1 = Arduino Uno (Rev3) - ICSP
  R1 = Resistor [tolerance=±5% power=0.25 resistance=220 package=THT]
  R2 = Resistor [tolerance=±5% power=0.25 resistance=220 package=THT]
  R3 = Resistor [tolerance=±5% power=0.25 resistance=220 package=THT]  # not connected
  RHT1 = Humidity and Temperature Sensor RHT03
  R4 = Resistor [tolerance=±5% power=0.25 resistance=220 package=THT]
  U3 = Barometric Pressure Sensor
  R5 = Resistor [tolerance=±5% power=0.25 resistance=220 package=THT]
  M1 = DC Motor

nets:
  N1: U1.+IN, U1.-V, U2.-V, P1.cathode, Composant1.GND, R1.Pin_1, R4.Pin_1, R5.Pin_1, M1.pin_2
  N2: U1.OUT, U2.+IN
  N3: U1.V+, U2.V+, Composant1.5V
  N4: U2.-IN, R1.Pin_0, R2.Pin_0
  N5: U2.OUT, Composant1.A0
  N6: Composant1.A2, M1.pin_1
  N7: Composant1.A4/SDA, U3.DRDY
  N8: Composant1.A5/SCL, U3.SCK
  N9: Composant1.D10_PWM/SS, RHT1.Data-signal
  3V3: Composant1.3V3, RHT1.Vcc, U3.3.3V
  N10: RHT1.GND_1, R4.Pin_0
  N11: U3.GND, R5.Pin_0
